# Fritzing sketch ds18x20 (saved by Fritzing 0.9.3b)

parts:
  U1 = NodeMCU V1.0
  DS1 = DS18B20 1-Wire Temperature Sensor [part_number=DS18B20]

nets:
  N1: U1.D0, U1.RST
  N2: U1.D3, DS1.DQ
  3V3: U1.3V3, DS1.VDD
  GND: U1.GND, DS1.GND

custom parts:
  NodeMCU V1.0: ESP8266 based NodeMCU
