# Fritzing sketch bme280 (saved by Fritzing 0.9.3b)

parts:
  U1 = NodeMCU V1.0
  U2 = Adafruit BME280

nets:
  N1: U1.D0, U1.RST
  N2: U1.D3, U2.SCK/SCL
  N3: U1.D4, U2.SDI/SDA
  3V3: U1.3V3, U2.VIN
  GND: U1.GND, U2.GND

custom parts:
  NodeMCU V1.0: ESP8266 based NodeMCU
  Adafruit BME280: Bosch has stepped up their game with their new BME280 sensor, an environmental sensor with temperature, barometric pressure and humidity! This sensor is great for all sorts of weather/environmental sensing and can even be used in both I2C and SPI! This precision sensor from Bosch is the best low-cost sensing solution for measuring humidity with ±3% accuracy, barometric pressure with ±1 hPa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
