# Fritzing sketch hc_sr501 (saved by Fritzing 0.9.3b)

parts:
  Bauteil1 = HC-SR501 Body Sensor Module
  U1 = NodeMCU V1.0

nets:
  N1: Bauteil1.VCC, U1.RSV#40
  N2: Bauteil1.OUT, U1.D2
  N3: Bauteil1.GND, U1.RSV#41

custom parts:
  HC-SR501 Body Sensor Module: Pyroelectric Infrared PIR Motion Sensor Detector Module
  NodeMCU V1.0: ESP8266 based NodeMCU
