# Fritzing sketch moisture (saved by Fritzing 0.9.3b)

parts:
  Bauteil1 = Soil Moisture Sensor
  WeMos_D1_Mini1 = WeMos D1 Mini

nets:
  N1: Bauteil1.GND, WeMos_D1_Mini1.G
  N2: Bauteil1.SIG, WeMos_D1_Mini1.A0
  VCC: Bauteil1.VCC, WeMos_D1_Mini1.3V3
  N3: WeMos_D1_Mini1.D0, WeMos_D1_Mini1.RST
